# Fritzing sketch schematic (saved by Fritzing 0.9.5d)

parts:
  U1 = NodeMCU V1.0
  Q1 = NPN-Transistor [part_number=BC337 package="TO92 [THT]"]
  LED1 = LED - 5mm [color="Infrared (940nm)" package="5 mm [THT]"]
  LED2 = LED - 3mm [color="Blue (505nm)" package="3 mm [THT]"]
  R1 = Resistor [tolerance=±5% resistance=10 package=THT]
  R2 = Resistor [tolerance=±5% resistance=150 package=THT]
  R3 = Resistor [tolerance=±5% resistance=68 package=THT]

nets:
  N1: U1.D2, R3.Pin_0
  N2: U1.GND, Q1.E
  N3: U1.Vin, R1.Pin_0, R2.Pin_0
  N4: Q1.B, R3.Pin_1
  N5: Q1.C, LED1.cathode, LED2.cathode
  N6: LED1.anode, R1.Pin_1
  N7: LED2.anode, R2.Pin_1

custom parts:
  NodeMCU V1.0: ESP8266 based NodeMCU
